# Fritzing sketch Untitled Sketch 2 (saved by Fritzing 0.9.3b)
breadboards: 1

parts:
  LED1 = LED - 5mm [color="Red (633nm)" package="5 mm [THT]"]
  R1 = Resistor [tolerance=±5% resistance=220 package=THT]
  V1 = DC Power [voltage=5]
  S1 = Pushbutton [package="[THT]"]

nets:
  N1: LED1.cathode, V1.V+
  N2: LED1.anode, R1.Pin_0
  N3: R1.Pin_1, S1.Pin_3, S1.Pin_4
  N4: V1.V-, S1.Pin_2
